# Fritzing sketch scheme (saved by Fritzing 0.9.3b)
stripboards: 1

parts:
  Часть1 = Arduino Nano (Rev3.0)
  DFRobot_DFPlayer_Mini1 = DFRobot DFPlayer Mini [part_number=DFR0299]
  A6_Module_Ver4 = IC, DIP package, 24 pins [chip_label="A6 GSM"]
  2_Channel_Relay1 = 2 Channel Power Relay
  Часть2 = LCD1602-I2C
  DS1 = DS18B20 1-Wire Temperature Sensor [part_number=DS18B20]
  DS2 = DS18B20 1-Wire Temperature Sensor [part_number=DS18B20]
  Power_plug2 = Power plug
  ENCODER1 = Rotary Encoder with Knob
  R3 = Resistor [tolerance=±5% resistance=4.7k package="1206 [SMD]"]
  R4 = Resistor [tolerance=±5% resistance=10k package="1206 [SMD]"]

nets:
  N1: Часть1.D2, A6_Module_Ver4.pin8
  N2: Часть1.D3, A6_Module_Ver4.pin9
  N3: Часть1.D7, DFRobot_DFPlayer_Mini1.TX
  N4: Часть1.D8, DFRobot_DFPlayer_Mini1.RX
  N5: Часть1.D9, R4.Pin_0
  N6: Часть1.D12/MISO, DS1.DQ, DS2.DQ, R3.Pin_0
  N7: Часть1.A5, Часть2.SCL
  N8: Часть1.A4, Часть2.SDA
  N9: Часть1.A2, ENCODER1.no_name_yet#4
  N10: Часть1.A1, ENCODER1.no_name_yet#1
  N11: Часть1.A0, ENCODER1.no_name_yet#3
  N12: Часть1.D13/SCK, 2_Channel_Relay1.IN1, 2_Channel_Relay1.IN2
  VCC: DFRobot_DFPlayer_Mini1.VCC, A6_Module_Ver4.pin1, 2_Channel_Relay1.VCC, DS1.VDD, DS2.VDD, Power_plug2.VCC, R3.Pin_1
  N13: DFRobot_DFPlayer_Mini1.DAC_R, A6_Module_Ver4.pin5
  GND: DFRobot_DFPlayer_Mini1.GND-1, DFRobot_DFPlayer_Mini1.GND-2, A6_Module_Ver4.pin2, 2_Channel_Relay1.GND, DS1.GND, DS2.GND, Power_plug2.GND, ENCODER1.no_name_yet#2, ENCODER1.no_name_yet#5
  N14: A6_Module_Ver4.pin13, R4.Pin_1

notes:
  4.7K
  RX
  TX
  PWR
  10K

custom parts:
  2 Channel Power Relay: A 2 channel power relay. The module operates at 5V.
  LCD1602-I2C: A standard character display, usually with 2x16 characters. Comes in many colors with LCM1602 IIC attached.
  Rotary Encoder with Knob: Rotary Encoder with 1/4" Shaft and Knob
